// Logisim project clock_sim.circ as structural Verilog: 1 circuit, main circuit main
module main (
);

  wire and_1_out, clock_1_out, counter_1_carry;
  wire [3:0] counter_1_q, counter_3_q;

  Clock clock_1 (.out(clock_1_out));
  Hex_Digit_Display hex_digit_display_1 (.value(counter_3_q));  // open: dp
  Counter #(.max('hf), .width(4)) counter_1 (
    .clr(and_1_out), .clk(clock_1_out), .carry(counter_1_carry), .Q(counter_1_q));  // open: load, up, count, D
  Hex_Digit_Display hex_digit_display_2 (.value(counter_1_q));  // open: dp
  Counter counter_2 (.up(1'b1), .clk(clock_1_out));  // open: clr, load, count, D, carry, Q
  Counter #(.max('hf), .width(4)) counter_3 (
    .clr(and_1_out), .clk(counter_1_carry), .Q(counter_3_q));  // open: load, up, count, D, carry
  and and_1 (and_1_out, counter_3_q[1], counter_3_q[0], counter_1_q[0], counter_1_q[1]);
endmodule
